// Digital circuit exbloc3b.dig as structural Verilog
module exbloc3b (
  input  A,
  input  D,
  input  C,
  input  B,
  output F
);

  wire not_1_out, undriven, undriven_2, undriven_3, undriven_4, undriven_5, undriven_6, undriven_7,
       undriven_8;

  not not_1 (not_1_out, A);
  Multiplexer #(.Selector_Bits(3)) multiplexer_1 (
    .sel({B, C, D}), .in_0(undriven), .in_1(undriven_2), .in_2(undriven_3), .in_3(undriven_4),
    .in_4(undriven_5), .in_5(undriven_6), .in_6(undriven_7), .in_7(undriven_8), .out(F));
endmodule
