// Digital circuit solExBloc3a.dig as structural Verilog
module solExBloc3a (
  input  z_0,
  input  z_1,
  input  y_0,
  input  y_1,
  input  y_2,
  output P_0,
  output P_1,
  output P_2,
  output P_3,
  output P_4
);

  wire add_2_c_o, add_3_c_o, add_4_c_o, and_1_out, and_2_out, and_3_out, and_4_out, and_5_out, and_6_out;

  and and_1 (and_1_out, y_2, z_1);
  and and_2 (and_2_out, y_2, z_0);
  and and_3 (and_3_out, y_1, z_1);
  and and_4 (and_4_out, y_1, z_0);
  and and_5 (and_5_out, y_0, z_1);
  and and_6 (and_6_out, y_0, z_0);
  Add add_1 (.a(and_1_out), .b(1'b0), .c_i(add_2_c_o), .s(P_3), .c_o(P_4));
  Add add_2 (.a(and_2_out), .b(and_3_out), .c_i(add_3_c_o), .s(P_2), .c_o(add_2_c_o));
  Add add_3 (.a(and_4_out), .b(and_5_out), .c_i(add_4_c_o), .s(P_1), .c_o(add_3_c_o));
  Add add_4 (.a(1'b0), .b(and_6_out), .c_i(1'b0), .s(P_0), .c_o(add_4_c_o));
endmodule
