// Digital circuit solReducKABC.dig as structural Verilog
module solReducKABC (
  input  A,
  input  B,
  input  C,
  output S
);

  wire and_1_out, and_2_out, not_1_out, not_2_out, or_1_out;

  not not_1 (not_1_out, A);
  not not_2 (not_2_out, B);
  or or_1 (or_1_out, A, C);
  and and_1 (and_1_out, not_1_out, not_2_out);
  and and_2 (and_2_out, B, or_1_out);
  or or_2 (S, and_1_out, and_2_out);
endmodule
